# Fritzing sketch KnightRiderv2 (saved by Fritzing 0.9.3b)
breadboards: 1

parts:
  Componente1 = Arduino Mega 2560 (Rev3)
  LED1 = LED - 3mm [color="Red (633nm)" package="3 mm [THT]"]
  LED2 = LED - 3mm [color="Red (633nm)" package="3 mm [THT]"]
  LED3 = LED - 3mm [color="Red (633nm)" package="3 mm [THT]"]
  LED4 = LED - 3mm [color="Red (633nm)" package="3 mm [THT]"]
  LED5 = LED - 3mm [color="Red (633nm)" package="3 mm [THT]"]
  LED6 = LED - 3mm [color="Red (633nm)" package="3 mm [THT]"]
  LED7 = LED - 3mm [color="Red (633nm)" package="3 mm [THT]"]
  LED8 = LED - 3mm [color="Red (633nm)" package="3 mm [THT]"]
  LED9 = LED - 3mm [color="Red (633nm)" package="3 mm [THT]"]
  R1 = Resistor [tolerance=±5% resistance=220 package="0402 [SMD]"]
  R2 = Resistor [tolerance=±5% resistance=220 package="0402 [SMD]"]
  R3 = Resistor [tolerance=±5% resistance=220 package="0402 [SMD]"]
  R4 = Resistor [tolerance=±5% resistance=220 package="0402 [SMD]"]
  R5 = Resistor [tolerance=±5% resistance=220 package="0402 [SMD]"]
  R6 = Resistor [tolerance=±5% resistance=220 package="0402 [SMD]"]
  R7 = Resistor [tolerance=±5% resistance=220 package="0402 [SMD]"]
  R8 = Resistor [tolerance=±5% resistance=220 package="0402 [SMD]"]
  R9 = Resistor [tolerance=±5% resistance=220 package="0402 [SMD]"]
  LED10 = LED - 3mm [color="Green (555nm)" package="3 mm [THT]"]
  R10 = Resistor [tolerance=±5% resistance=220 package="0402 [SMD]"]
  J1 = Piezo Speaker
  S1 = Momentary Switch [package=ksa_sealed_tac_switch]
  R11 = Resistor [tolerance=±5% resistance=10k package="0402 [SMD]"]

nets:
  N1: Componente1.D13_PWM, S1.3
  N2: Componente1.D12_PWM, LED1.anode
  N3: Componente1.D11_PWM, LED6.anode
  N4: Componente1.D10_PWM, LED7.anode
  N5: Componente1.D9_PWM, LED8.anode
  N6: Componente1.D8_PWM, LED9.anode
  N7: Componente1.5V, S1.2
  N8: Componente1.GND, R1.Pin_1, R2.Pin_1, R3.Pin_1, R4.Pin_1, R5.Pin_1, R6.Pin_1, R7.Pin_1, R8.Pin_1, R9.Pin_1, R10.Pin_0, J1.pin1, R11.Pin_1
  N9: Componente1.D2_PWM, LED10.anode
  N10: Componente1.D3_PWM, J1.pin2
  N11: Componente1.D4_PWM, LED5.anode
  N12: Componente1.D5_PWM, LED4.anode
  N13: Componente1.D6_PWM, LED3.anode
  N14: Componente1.D7_PWM, LED2.anode
  N15: LED1.cathode, R9.Pin_0
  N16: LED2.cathode, R4.Pin_0
  N17: LED3.cathode, R3.Pin_0
  N18: LED4.cathode, R2.Pin_0
  N19: LED5.cathode, R1.Pin_0
  N20: LED6.cathode, R8.Pin_0
  N21: LED7.cathode, R7.Pin_0
  N22: LED8.cathode, R6.Pin_0
  N23: LED9.cathode, R5.Pin_0
  N24: LED10.cathode, R10.Pin_1
  N25: S1.4, R11.Pin_0
