# Fritzing sketch LCD_RTC_DHT11_Boton (saved by Fritzing 0.9.3b)
breadboards: 1

parts:
  DHT1 = DHT11_Temperature_and_Humitidy_Sensor
  Componente1 = Arduino Mega 2560 (Rev3)
  Componente2 = LCD1602-I2C_
  PCB2 = RTC_DS1302_module
  S1 = Momentary Switch [package=ksa_sealed_tac_switch]
  R1 = Resistor [tolerance=±5% resistance=10k package="1206 [SMD]"]

nets:
  N1: DHT1.connector2, Componente1.D6_PWM
  N2: DHT1.connector4, Componente1.GND, Componente2.connector0, PCB2.connector3, R1.Pin_1
  N3: Componente1.D21/SCL, Componente2.connector3
  N4: Componente1.D20/SDA, Componente2.connector2
  N5: Componente1.3V3, PCB2.connector0
  N6: Componente1.5V, Componente2.connector1, S1.1
  N7: Componente1.D2_PWM, PCB2.connector6
  N8: Componente1.D3_PWM, PCB2.connector5
  N9: Componente1.D4_PWM, PCB2.connector4
  N10: Componente1.D5_PWM, S1.4
  N11: S1.3, R1.Pin_0
